// Logisim project PC.circ as structural Verilog: 2 circuits, main circuit PC
module PC (
  input  ENABLE,
  input  CLK,
  input  RESET
);

  wire bridge_1_read_ram, bridge_1_sel_cmos, bridge_1_sel_mmio, bridge_1_sel_ram, cpu_1_mwe, decoder_1_out49,
       pull_resistor_1_node, pull_resistor_2_node;
  wire [3:0] cpu_1_le0;
  wire [7:0] pla_1_out, rom_1_p1, rom_1_p2, rom_1_p3, rom_1_p4, undriven, undriven_2, undriven_3, undriven_4,
       undriven_5, undriven_6, undriven_7, undriven_8, undriven_9, undriven_10, undriven_11, undriven_12,
       undriven_13, undriven_14, undriven_15, undriven_16, undriven_17, undriven_18, undriven_19,
       undriven_20, undriven_21, undriven_22, undriven_23, undriven_24;
  wire [15:0] cpu_1_addr_out;
  wire [31:0] controlled_buffer_3_out, cpu_1_data_out, cpu_1_ic_out, multiplexer_2_out, multiplexer_3_out,
       multiplexer_4_out;
  wire [31:16] cpu_1_addr_out_2;
  wire [63:0] multiplexer_1_out;

  TTY #(.cols(80), .rows(24)) tty_1 (.data(cpu_1_data_out[6:0]), .clk(CLK), .we(bridge_1_sel_mmio), .clr(RESET));
  Multiplexer #(.width(64)) multiplexer_1 (
    .in0({undriven_8, undriven_7, undriven_6, undriven_5, undriven_4, undriven_3, undriven_2, undriven}),
    .in1({undriven_16, undriven_15, undriven_14, undriven_13, undriven_12, undriven_11, undriven_10, undriven_9}),
    .out(multiplexer_1_out), .sel(bridge_1_read_ram));
  CPU cpu_1 (
    .INST_IN(multiplexer_1_out), .DATA_IN(multiplexer_4_out), .ENABLE(ENABLE), .CLK(CLK), .RESET(RESET),
    .LE0(cpu_1_le0[0]), .LE1(cpu_1_le0[1]), .LE2(cpu_1_le0[2]), .LE3(cpu_1_le0[3]),
    .DATA_OUT(cpu_1_data_out), .MWE(cpu_1_mwe), .ADDR_OUT({cpu_1_addr_out_2, cpu_1_addr_out}),
    .IC_OUT(cpu_1_ic_out));  // open: INT_IN, CALL_IRQ, MOE, FLAGS_OUT, IRQ_EN
  BRIDGE bridge_1 (
    .INST_ADDR_IN(cpu_1_ic_out), .DATA_ADDR_IN({cpu_1_addr_out_2, cpu_1_addr_out}),
    .READ_RAM(bridge_1_read_ram), .SEL_CMOS(bridge_1_sel_cmos), .SEL_MMIO(bridge_1_sel_mmio),
    .SEL_RAM(bridge_1_sel_ram));  // open: SEL_BIOS
  PLA #(.in_width(16), .out_width(8), .\table ("0000011100000000 00110001 # MEM_SIZE")) pla_1 (
    .in(cpu_1_addr_out), .out(pla_1_out));
  Decoder #(.select(6)) decoder_1 (
    .out49(decoder_1_out49), .sel(pla_1_out[5:0]), .en(bridge_1_sel_mmio));  // open: out0, out1, out2, out3, out4, out5, out6, out7, out8, out9, out10, out11, out12, out13, out14, out15, out16, out17, out18, out19, out20, out21, out22, out23, out24, out25, out26, out27, out28, out29, out30, out31, out32, out33, out34, out35, out36, out37, out38, out39, out40, out41, out42, out43, out44, out45, out46, out47, out48, out50, out51, out52, out53, out54, out55, out56, out57, out58, out59, out60, out61, out62, out63
  Pull_Resistor pull_resistor_1 (.node(pull_resistor_1_node));
  assign pull_resistor_1_node = bridge_1_sel_cmos ? cpu_1_mwe : 1'bz;  // Controlled_Buffer controlled_buffer_1
  Pull_Resistor pull_resistor_2 (.node(pull_resistor_2_node));
  assign pull_resistor_2_node = bridge_1_sel_ram ? cpu_1_mwe : 1'bz;  // Controlled_Buffer controlled_buffer_2
  // ROM #(.addrWidth(16), .line("octo"), .misaligned("true")) BIOS: pin names not known
  // ROM #(.addrWidth(16), .line("quad"), .misaligned("true")) rom_1: pin names not known; wires that end beside it: rom_1_p1, rom_1_p2, rom_1_p3, rom_1_p4
  // RAM #(.addrWidth(16), .enables("line"), .line("quad"), .misaligned("true")) CMOS_RAM: pin names not known; wires that end beside it: pull_resistor_1_node, CLK
  // DualRAM #(.addrWidth(24), .clearpin("true"), .enables("line"), .line("octo"), .misaligned("true")) DRAM: pin names not known; wires that end beside it: cpu_1_ic_out[23:0], CLK, {cpu_1_addr_out_2[23:16], cpu_1_addr_out}, pull_resistor_2_node, RESET
  Multiplexer #(.width(32)) multiplexer_2 (
    .in0({rom_1_p1, rom_1_p2, rom_1_p3, rom_1_p4}),
    .in1({undriven_20, undriven_19, undriven_18, undriven_17}), .out(multiplexer_2_out),
    .sel(bridge_1_sel_cmos));
  assign controlled_buffer_3_out = decoder_1_out49 ? 32'hffffff : 32'bz;  // Controlled_Buffer controlled_buffer_3
  Multiplexer #(.width(32)) multiplexer_3 (
    .in0(multiplexer_2_out), .in1({undriven_24, undriven_23, undriven_22, undriven_21}),
    .out(multiplexer_3_out), .sel(bridge_1_sel_ram));
  Multiplexer #(.width(32)) multiplexer_4 (
    .in0(multiplexer_3_out), .in1(controlled_buffer_3_out), .out(multiplexer_4_out), .sel(bridge_1_sel_mmio));
  Pull_Resistor pull_resistor_3 (.node(controlled_buffer_3_out));

  // Notes on the sheet:
  //   contents of BIOS (hex, n*v repeats v):
  //   27 21 3 18 ff 0 0 0 21 1 f 20 22 0 f 0 2 0 0 1c 1 f 7e c f 1e c ff ff ff ed 1
endmodule

module BRIDGE (
  input  [31:0] INST_ADDR_IN,
  input  [31:0] DATA_ADDR_IN,
  output READ_RAM,
  output SEL_BIOS,
  output SEL_CMOS,
  output SEL_MMIO,
  output SEL_RAM
);

  wire comparator_1_eq, comparator_1_gt, comparator_2_eq, comparator_2_gt, comparator_3_eq, comparator_3_lt,
       comparator_4_eq, comparator_4_gt, comparator_5_eq, comparator_5_lt, comparator_6_eq, comparator_6_gt,
       comparator_7_eq, comparator_7_lt, comparator_8_eq, comparator_8_gt, comparator_9_eq, comparator_9_lt,
       or_2_out, or_3_out, or_4_out, or_5_out, or_6_out, or_7_out, or_8_out, or_9_out;

  or or_1 (READ_RAM, comparator_1_gt, comparator_1_eq);
  Comparator #(.mode("unsigned"), .width(32)) comparator_1 (
    .a(INST_ADDR_IN), .b(32'h10000), .gt(comparator_1_gt), .eq(comparator_1_eq));  // open: lt
  or or_2 (or_2_out, comparator_2_gt, comparator_2_eq);
  Comparator #(.mode("unsigned"), .width(32)) comparator_2 (
    .a(DATA_ADDR_IN), .b({32{1'b0}}), .gt(comparator_2_gt), .eq(comparator_2_eq));  // open: lt
  and and_1 (SEL_BIOS, or_2_out, or_3_out);
  or or_3 (or_3_out, comparator_3_eq, comparator_3_lt);
  Comparator #(.mode("unsigned"), .width(32)) comparator_3 (
    .a(DATA_ADDR_IN), .b(32'hffff), .eq(comparator_3_eq), .lt(comparator_3_lt));  // open: gt
  or or_4 (or_4_out, comparator_4_gt, comparator_4_eq);
  Comparator #(.mode("unsigned"), .width(32)) comparator_4 (
    .a(DATA_ADDR_IN), .b(32'h10000), .gt(comparator_4_gt), .eq(comparator_4_eq));  // open: lt
  and and_2 (SEL_CMOS, or_4_out, or_5_out);
  or or_5 (or_5_out, comparator_5_eq, comparator_5_lt);
  Comparator #(.mode("unsigned"), .width(32)) comparator_5 (
    .a(DATA_ADDR_IN), .b(32'h1ffff), .eq(comparator_5_eq), .lt(comparator_5_lt));  // open: gt
  or or_6 (or_6_out, comparator_6_gt, comparator_6_eq);
  Comparator #(.mode("unsigned"), .width(32)) comparator_6 (
    .a(DATA_ADDR_IN), .b(32'h20000), .gt(comparator_6_gt), .eq(comparator_6_eq));  // open: lt
  and and_3 (SEL_MMIO, or_6_out, or_7_out);
  or or_7 (or_7_out, comparator_7_eq, comparator_7_lt);
  Comparator #(.mode("unsigned"), .width(32)) comparator_7 (
    .a(DATA_ADDR_IN), .b(32'h2ffff), .eq(comparator_7_eq), .lt(comparator_7_lt));  // open: gt
  or or_8 (or_8_out, comparator_8_gt, comparator_8_eq);
  Comparator #(.mode("unsigned"), .width(32)) comparator_8 (
    .a(DATA_ADDR_IN), .b(32'h30000), .gt(comparator_8_gt), .eq(comparator_8_eq));  // open: lt
  and and_4 (SEL_RAM, or_8_out, or_9_out);
  or or_9 (or_9_out, comparator_9_eq, comparator_9_lt);
  Comparator #(.mode("unsigned"), .width(32)) comparator_9 (
    .a(DATA_ADDR_IN), .b({32{1'b1}}), .eq(comparator_9_eq), .lt(comparator_9_lt));  // open: gt
endmodule
