// Logisim project i80148.circ as structural Verilog
module CPU (
  input  [31:0] DATA_IN
);
endmodule

module REGFILE (
  input  [31:0] DATA_IN,
  input  [5:0] REG_WR,
  input  [5:0] REG_A,
  input  [5:0] REG_B,
  input  [5:0] REG_C,
  input  WE,
  input  CLK,
  input  RESET,
  output [3:0] MODE,
  output [31:0] A,
  output [31:0] B,
  output [31:0] C
);

  wire and_1_out, and_2_out, and_3_out, and_4_out, and_5_out, and_6_out, and_7_out, and_8_out, and_9_out,
       and_10_out, and_11_out, and_12_out, and_13_out, and_14_out, and_15_out, and_16_out, and_17_out,
       and_18_out, and_19_out, and_20_out, and_21_out, and_22_out, and_23_out, and_24_out, and_25_out,
       and_26_out, and_27_out, and_28_out, and_29_out, and_30_out, and_31_out, and_32_out, decoder_1_out1,
       decoder_1_out2, decoder_1_out3, decoder_1_out4, decoder_1_out5, decoder_1_out6, decoder_1_out7,
       decoder_1_out8, decoder_1_out9, decoder_1_out10, decoder_1_out11, decoder_1_out12, decoder_1_out13,
       decoder_1_out14, decoder_1_out15, decoder_1_out16, decoder_1_out17, decoder_1_out18, decoder_1_out19,
       decoder_1_out20, decoder_1_out21, decoder_1_out25, decoder_1_out26, decoder_1_out27, decoder_1_out28,
       decoder_1_out29, decoder_1_out30, decoder_1_out31, decoder_1_out32, decoder_1_out33, decoder_1_out34,
       decoder_1_out35, or_1_out, or_2_out, or_3_out, or_4_out, or_5_out, or_6_out, or_7_out, or_8_out,
       or_9_out, or_10_out, or_11_out, or_12_out, or_13_out, or_14_out;
  wire [7:0] pull_resistor_7_node, pull_resistor_7_node_3, X1_q, X2_q, X3_q, X4_q, X5_q, X6_q, XL1_q, XL2_q,
       XL3_q, XL4_q, XL5_q, XL6_q;
  wire [15:0] EX1_q, EX2_q, EX3_q, EX4_q, EX5_q, EX6_q, EX7_q;
  wire [31:0] A0_q, A1_q, A2_q, A3_q, A4_q, A5_q, A6_q, A7_q, BP_q, IX_q, IY_q, pull_resistor_15_node,
       pull_resistor_16_node, pull_resistor_17_node, undriven, undriven_2, undriven_3;
  wire [31:8] pull_resistor_8_node, pull_resistor_9_node, pull_resistor_10_node, pull_resistor_11_node,
       pull_resistor_12_node, pull_resistor_13_node, pull_resistor_14_node;
  wire [31:16] pull_resistor_1_node, pull_resistor_2_node, pull_resistor_3_node, pull_resistor_4_node,
       pull_resistor_5_node, pull_resistor_6_node, pull_resistor_7_node_2;

  ROM #(.addrWidth(6), .dataWidth(4)) rom_1 (.addr(REG_WR), .data(MODE));
  Decoder #(.select(6)) decoder_1 (
    .out1(decoder_1_out1), .out2(decoder_1_out2), .out3(decoder_1_out3), .out4(decoder_1_out4),
    .out5(decoder_1_out5), .out6(decoder_1_out6), .out7(decoder_1_out7), .out8(decoder_1_out8),
    .out9(decoder_1_out9), .out10(decoder_1_out10), .out11(decoder_1_out11), .out12(decoder_1_out12),
    .out13(decoder_1_out13), .out14(decoder_1_out14), .out15(decoder_1_out15), .out16(decoder_1_out16),
    .out17(decoder_1_out17), .out18(decoder_1_out18), .out19(decoder_1_out19), .out20(decoder_1_out20),
    .out21(decoder_1_out21), .out25(decoder_1_out25), .out26(decoder_1_out26), .out27(decoder_1_out27),
    .out28(decoder_1_out28), .out29(decoder_1_out29), .out30(decoder_1_out30), .out31(decoder_1_out31),
    .out32(decoder_1_out32), .out33(decoder_1_out33), .out34(decoder_1_out34), .out35(decoder_1_out35),
    .sel(REG_WR));  // open: out0, out22, out23, out24, out36, out37, out38, out39, out40, out41, out42, out43, out44, out45, out46, out47, out48, out49, out50, out51, out52, out53, out54, out55, out56, out57, out58, out59, out60, out61, out62, out63, en
  or or_1 (or_1_out, decoder_1_out15, decoder_1_out8, decoder_1_out1);
  or or_2 (or_2_out, decoder_1_out8, decoder_1_out1);
  Register XL1 (.D(DATA_IN[7:0]), .en(and_1_out), .clk(CLK), .Q(XL1_q), .clr(RESET));
  and and_1 (and_1_out, WE, or_1_out);
  Register X1 (.D(DATA_IN[15:8]), .en(and_2_out), .clk(CLK), .Q(X1_q), .clr(RESET));
  and and_2 (and_2_out, WE, or_2_out);
  Register #(.width(16)) EX1 (.D(DATA_IN[31:16]), .en(and_3_out), .clk(CLK), .Q(EX1_q), .clr(RESET));
  and and_3 (and_3_out, WE, decoder_1_out1);
  Register #(.width(32)) IX (.D(DATA_IN), .en(and_4_out), .clk(CLK), .Q(IX_q), .clr(RESET));
  and and_4 (and_4_out, WE, decoder_1_out26);
  Register #(.width(32)) IY (.D(DATA_IN), .en(and_5_out), .clk(CLK), .Q(IY_q), .clr(RESET));
  and and_5 (and_5_out, WE, decoder_1_out27);
  or or_3 (or_3_out, decoder_1_out16, decoder_1_out9, decoder_1_out2);
  or or_4 (or_4_out, decoder_1_out9, decoder_1_out2);
  Register XL2 (.D(DATA_IN[7:0]), .en(and_6_out), .clk(CLK), .Q(XL2_q), .clr(RESET));
  and and_6 (and_6_out, WE, or_3_out);
  Register X2 (.D(DATA_IN[15:8]), .en(and_7_out), .clk(CLK), .Q(X2_q), .clr(RESET));
  and and_7 (and_7_out, WE, or_4_out);
  Register #(.width(16)) EX2 (.D(DATA_IN[31:16]), .en(and_8_out), .clk(CLK), .Q(EX2_q), .clr(RESET));
  and and_8 (and_8_out, WE, decoder_1_out2);
  Register #(.width(32)) A0 (.D(DATA_IN), .en(and_9_out), .clk(CLK), .Q(A0_q), .clr(RESET));
  and and_9 (and_9_out, WE, decoder_1_out28);
  Register #(.width(32)) A4 (.D(DATA_IN), .en(and_10_out), .clk(CLK), .Q(A4_q), .clr(RESET));
  and and_10 (and_10_out, WE, decoder_1_out32);
  and and_11 (and_11_out, WE, or_5_out);
  or or_5 (or_5_out, decoder_1_out17, decoder_1_out10, decoder_1_out3);
  and and_12 (and_12_out, WE, or_6_out);
  or or_6 (or_6_out, decoder_1_out10, decoder_1_out3);
  and and_13 (and_13_out, WE, decoder_1_out3);
  and and_14 (and_14_out, WE, decoder_1_out29);
  and and_15 (and_15_out, WE, decoder_1_out33);
  Register XL3 (.D(DATA_IN[7:0]), .en(and_11_out), .clk(CLK), .Q(XL3_q), .clr(RESET));
  Register X3 (.D(DATA_IN[15:8]), .en(and_12_out), .clk(CLK), .Q(X3_q), .clr(RESET));
  Register #(.width(16)) EX3 (.D(DATA_IN[31:16]), .en(and_13_out), .clk(CLK), .Q(EX3_q), .clr(RESET));
  Register #(.width(32)) A1 (.D(DATA_IN), .en(and_14_out), .clk(CLK), .Q(A1_q), .clr(RESET));
  Register #(.width(32)) A5 (.D(DATA_IN), .en(and_15_out), .clk(CLK), .Q(A5_q), .clr(RESET));
  or or_7 (or_7_out, decoder_1_out18, decoder_1_out11, decoder_1_out4);
  or or_8 (or_8_out, decoder_1_out11, decoder_1_out4);
  Register XL4 (.D(DATA_IN[7:0]), .en(and_16_out), .clk(CLK), .Q(XL4_q), .clr(RESET));
  and and_16 (and_16_out, WE, or_7_out);
  Register X4 (.D(DATA_IN[15:8]), .en(and_17_out), .clk(CLK), .Q(X4_q), .clr(RESET));
  and and_17 (and_17_out, WE, or_8_out);
  Register #(.width(16)) EX4 (.D(DATA_IN[31:16]), .en(and_18_out), .clk(CLK), .Q(EX4_q), .clr(RESET));
  and and_18 (and_18_out, WE, decoder_1_out4);
  Register #(.width(32)) A2 (.D(DATA_IN), .en(and_19_out), .clk(CLK), .Q(A2_q), .clr(RESET));
  and and_19 (and_19_out, WE, decoder_1_out30);
  Register #(.width(32)) A6 (.D(DATA_IN), .en(and_20_out), .clk(CLK), .Q(A6_q), .clr(RESET));
  and and_20 (and_20_out, WE, decoder_1_out34);
  and and_21 (and_21_out, WE, or_9_out);
  or or_9 (or_9_out, decoder_1_out19, decoder_1_out12, decoder_1_out5);
  and and_22 (and_22_out, WE, or_10_out);
  or or_10 (or_10_out, decoder_1_out12, decoder_1_out5);
  and and_23 (and_23_out, WE, decoder_1_out5);
  and and_24 (and_24_out, WE, decoder_1_out31);
  and and_25 (and_25_out, WE, decoder_1_out35);
  Register XL5 (.D(DATA_IN[7:0]), .en(and_21_out), .clk(CLK), .Q(XL5_q), .clr(RESET));
  Register X5 (.D(DATA_IN[15:8]), .en(and_22_out), .clk(CLK), .Q(X5_q), .clr(RESET));
  Register #(.width(16)) EX5 (.D(DATA_IN[31:16]), .en(and_23_out), .clk(CLK), .Q(EX5_q), .clr(RESET));
  Register #(.width(32)) A3 (.D(DATA_IN), .en(and_24_out), .clk(CLK), .Q(A3_q), .clr(RESET));
  Register #(.width(32)) A7 (.D(DATA_IN), .en(and_25_out), .clk(CLK), .Q(A7_q), .clr(RESET));
  or or_11 (or_11_out, decoder_1_out20, decoder_1_out13, decoder_1_out6);
  or or_12 (or_12_out, decoder_1_out13, decoder_1_out6);
  Register XL6 (.D(DATA_IN[7:0]), .en(and_26_out), .clk(CLK), .Q(XL6_q), .clr(RESET));
  and and_26 (and_26_out, WE, or_11_out);
  Register X6 (.D(DATA_IN[15:8]), .en(and_27_out), .clk(CLK), .Q(X6_q), .clr(RESET));
  and and_27 (and_27_out, WE, or_12_out);
  Register #(.width(16)) EX6 (.D(DATA_IN[31:16]), .en(and_28_out), .clk(CLK), .Q(EX6_q), .clr(RESET));
  and and_28 (and_28_out, WE, decoder_1_out6);
  Register #(.width(32)) BP (.D(DATA_IN), .en(and_29_out), .clk(CLK), .Q(BP_q), .clr(RESET));
  and and_29 (and_29_out, WE, decoder_1_out25);
  Pull_Resistor pull_resistor_1 (.node({pull_resistor_1_node, X1_q, XL1_q}));
  Pull_Resistor pull_resistor_2 (.node({pull_resistor_2_node, X2_q, XL2_q}));
  Pull_Resistor pull_resistor_3 (.node({pull_resistor_3_node, X3_q, XL3_q}));
  Pull_Resistor pull_resistor_4 (.node({pull_resistor_4_node, X4_q, XL4_q}));
  Pull_Resistor pull_resistor_5 (.node({pull_resistor_5_node, X5_q, XL5_q}));
  Pull_Resistor pull_resistor_6 (.node({pull_resistor_6_node, X6_q, XL6_q}));
  Pull_Resistor pull_resistor_7 (.node({pull_resistor_7_node_2, pull_resistor_7_node, pull_resistor_7_node_3}));
  Pull_Resistor pull_resistor_8 (.node({pull_resistor_8_node, XL1_q}));
  Pull_Resistor pull_resistor_9 (.node({pull_resistor_9_node, XL2_q}));
  Pull_Resistor pull_resistor_10 (.node({pull_resistor_10_node, XL3_q}));
  Pull_Resistor pull_resistor_11 (.node({pull_resistor_11_node, XL4_q}));
  Pull_Resistor pull_resistor_12 (.node({pull_resistor_12_node, XL5_q}));
  Pull_Resistor pull_resistor_13 (.node({pull_resistor_13_node, XL6_q}));
  Pull_Resistor pull_resistor_14 (.node({pull_resistor_14_node, pull_resistor_7_node_3}));
  or or_13 (or_13_out, decoder_1_out21, decoder_1_out14, decoder_1_out7);
  or or_14 (or_14_out, decoder_1_out14, decoder_1_out7);
  Register XL7 (.D(DATA_IN[7:0]), .en(and_30_out), .clk(CLK), .Q(pull_resistor_7_node_3), .clr(RESET));
  and and_30 (and_30_out, WE, or_13_out);
  Register X7 (.D(DATA_IN[15:8]), .en(and_31_out), .clk(CLK), .Q(pull_resistor_7_node), .clr(RESET));
  and and_31 (and_31_out, WE, or_14_out);
  Register #(.width(16)) EX7 (.D(DATA_IN[31:16]), .en(and_32_out), .clk(CLK), .Q(EX7_q), .clr(RESET));
  and and_32 (and_32_out, WE, decoder_1_out7);
  Pull_Resistor pull_resistor_15 (.node(pull_resistor_15_node));
  Multiplexer #(.select(6), .width(32)) multiplexer_1 (
    .in0(pull_resistor_15_node), .in1({EX1_q, X1_q, XL1_q}), .in2({EX2_q, X2_q, XL2_q}),
    .in3({EX3_q, X3_q, XL3_q}), .in4({EX4_q, X4_q, XL4_q}), .in5({EX5_q, X5_q, XL5_q}),
    .in6({EX6_q, X6_q, XL6_q}), .in7({EX7_q, pull_resistor_7_node, pull_resistor_7_node_3}),
    .in8({pull_resistor_1_node, X1_q, XL1_q}), .in9({pull_resistor_2_node, X2_q, XL2_q}),
    .in10({pull_resistor_3_node, X3_q, XL3_q}), .in11({pull_resistor_4_node, X4_q, XL4_q}),
    .in12({pull_resistor_5_node, X5_q, XL5_q}), .in13({pull_resistor_6_node, X6_q, XL6_q}),
    .in14({pull_resistor_7_node_2, pull_resistor_7_node, pull_resistor_7_node_3}),
    .in15({pull_resistor_8_node, XL1_q}), .in16({pull_resistor_9_node, XL2_q}),
    .in17({pull_resistor_10_node, XL3_q}), .in18({pull_resistor_11_node, XL4_q}),
    .in19({pull_resistor_12_node, XL5_q}), .in20({pull_resistor_13_node, XL6_q}),
    .in21({pull_resistor_14_node, pull_resistor_7_node_3}), .in22(undriven), .in23(undriven_2),
    .in24(undriven_3), .in25(BP_q), .in26(IX_q), .in27(IY_q), .in28(A0_q), .in29(A1_q), .in30(A2_q),
    .in31(A3_q), .in32(A4_q), .in33(A5_q), .in34(A6_q), .in35(A7_q), .out(A), .sel(REG_A));  // open: in36, in37, in38, in39, in40, in41, in42, in43, in44, in45, in46, in47, in48, in49, in50, in51, in52, in53, in54, in55, in56, in57, in58, in59, in60, in61, in62, in63
  Pull_Resistor pull_resistor_16 (.node(pull_resistor_16_node));
  Pull_Resistor pull_resistor_17 (.node(pull_resistor_17_node));
  Multiplexer #(.select(6), .width(32)) multiplexer_2 (
    .in0(pull_resistor_16_node), .in1({EX1_q, X1_q, XL1_q}), .in2({EX2_q, X2_q, XL2_q}),
    .in3({EX3_q, X3_q, XL3_q}), .in4({EX4_q, X4_q, XL4_q}), .in5({EX5_q, X5_q, XL5_q}),
    .in6({EX6_q, X6_q, XL6_q}), .in7({EX7_q, pull_resistor_7_node, pull_resistor_7_node_3}),
    .in8({pull_resistor_1_node, X1_q, XL1_q}), .in9({pull_resistor_2_node, X2_q, XL2_q}),
    .in10({pull_resistor_3_node, X3_q, XL3_q}), .in11({pull_resistor_4_node, X4_q, XL4_q}),
    .in12({pull_resistor_5_node, X5_q, XL5_q}), .in13({pull_resistor_6_node, X6_q, XL6_q}),
    .in14({pull_resistor_7_node_2, pull_resistor_7_node, pull_resistor_7_node_3}),
    .in15({pull_resistor_8_node, XL1_q}), .in16({pull_resistor_9_node, XL2_q}),
    .in17({pull_resistor_10_node, XL3_q}), .in18({pull_resistor_11_node, XL4_q}),
    .in19({pull_resistor_12_node, XL5_q}), .in20({pull_resistor_13_node, XL6_q}),
    .in21({pull_resistor_14_node, pull_resistor_7_node_3}), .in22(undriven), .in23(undriven_2),
    .in24(undriven_3), .in25(BP_q), .in26(IX_q), .in27(IY_q), .in28(A0_q), .in29(A1_q), .in30(A2_q),
    .in31(A3_q), .in32(A4_q), .in33(A5_q), .in34(A6_q), .in35(A7_q), .out(B), .sel(REG_B));  // open: in36, in37, in38, in39, in40, in41, in42, in43, in44, in45, in46, in47, in48, in49, in50, in51, in52, in53, in54, in55, in56, in57, in58, in59, in60, in61, in62, in63
  Multiplexer #(.select(6), .width(32)) multiplexer_3 (
    .in0(pull_resistor_17_node), .in1({EX1_q, X1_q, XL1_q}), .in2({EX2_q, X2_q, XL2_q}),
    .in3({EX3_q, X3_q, XL3_q}), .in4({EX4_q, X4_q, XL4_q}), .in5({EX5_q, X5_q, XL5_q}),
    .in6({EX6_q, X6_q, XL6_q}), .in7({EX7_q, pull_resistor_7_node, pull_resistor_7_node_3}),
    .in8({pull_resistor_1_node, X1_q, XL1_q}), .in9({pull_resistor_2_node, X2_q, XL2_q}),
    .in10({pull_resistor_3_node, X3_q, XL3_q}), .in11({pull_resistor_4_node, X4_q, XL4_q}),
    .in12({pull_resistor_5_node, X5_q, XL5_q}), .in13({pull_resistor_6_node, X6_q, XL6_q}),
    .in14({pull_resistor_7_node_2, pull_resistor_7_node, pull_resistor_7_node_3}),
    .in15({pull_resistor_8_node, XL1_q}), .in16({pull_resistor_9_node, XL2_q}),
    .in17({pull_resistor_10_node, XL3_q}), .in18({pull_resistor_11_node, XL4_q}),
    .in19({pull_resistor_12_node, XL5_q}), .in20({pull_resistor_13_node, XL6_q}),
    .in21({pull_resistor_14_node, pull_resistor_7_node_3}), .in22(undriven), .in23(undriven_2),
    .in24(undriven_3), .in25(BP_q), .in26(IX_q), .in27(IY_q), .in28(A0_q), .in29(A1_q), .in30(A2_q),
    .in31(A3_q), .in32(A4_q), .in33(A5_q), .in34(A6_q), .in35(A7_q), .out(C), .sel(REG_C));  // open: in36, in37, in38, in39, in40, in41, in42, in43, in44, in45, in46, in47, in48, in49, in50, in51, in52, in53, in54, in55, in56, in57, in58, in59, in60, in61, in62, in63

  // Notes on the sheet:
  //   contents of rom_1 (hex, n*v repeats v):
  //   0 7*2 7*1 7*0 2 0 12*2
endmodule

module ALU (
  input  [31:0] A,
  input  [31:0] B,
  input  CARRY,
  input  BORROW,
  input  [3:0] OP,
  input  SET_SIGNED,
  input  SET_REM,
  input  [3:0] MODE,
  input  ALU_EN,
  output BORROW_OUT,
  output CARRY_OUT,
  output [31:0] RESULT,
  output ZERO_OUT,
  output SIGN_OUT,
  output GREATER_OUT,
  output EQUALS_OUT,
  output LESS_OUT
);

  wire adder_1_cout, multiplexer_1_out, multiplexer_2_out, subtractor_1_bout;
  wire [2:0] comparator_1_gt, comparator_2_gt, comparator_3_gt, comparator_4_gt, comparator_5_gt,
       comparator_6_gt, multiplexer_6_out, multiplexer_7_out, multiplexer_8_out, multiplexer_12_out;
  wire [31:0] adder_1_out, and_1_out, divider_1_out, divider_1_rem, divider_2_out, divider_2_rem,
       multiplexer_3_out, multiplexer_4_out, multiplexer_5_out, multiplexer_11_out, multiplier_1_out,
       multiplier_2_out, not_1_out, or_1_out, shifter_1_out, shifter_2_out, shifter_3_out, shifter_4_out,
       shifter_5_out, subtractor_1_out, xor_1_out;

  Adder #(.width(32)) adder_1 (.a(A), .b(B), .out(adder_1_out), .cin(CARRY), .cout(adder_1_cout));
  Subtractor #(.width(32)) subtractor_1 (.a(A), .b(B), .out(subtractor_1_out), .bin(BORROW), .bout(subtractor_1_bout));
  Multiplier #(.width(32)) multiplier_1 (.a(A), .b(B), .out(multiplier_1_out));  // open: cin, cout
  Multiplier #(.mode("twosComplement"), .width(32)) multiplier_2 (
    .a(A), .b(B), .out(multiplier_2_out));  // open: cin, cout
  Divider #(.width(32)) divider_1 (.a(A), .b(B), .out(divider_1_out), .rem(divider_1_rem));  // open: upper
  Divider #(.mode("twosComplement"), .width(32)) divider_2 (
    .a(A), .b(B), .out(divider_2_out), .rem(divider_2_rem));  // open: upper
  assign not_1_out = ~A;  // NOT_Gate not_1, 32 bits wide
  assign and_1_out = A & B;  // AND_Gate and_1, 32 bits wide
  assign or_1_out = A | B;  // OR_Gate or_1, 32 bits wide
  assign xor_1_out = A ^ B;  // XOR_Gate xor_1, 32 bits wide
  Shifter #(.width(32)) shifter_1 (.in(A), .\dist (B[4:0]), .out(shifter_1_out));
  Shifter #(.shift("lr"), .width(32)) shifter_2 (.in(A), .\dist (B[4:0]), .out(shifter_2_out));
  Shifter #(.shift("ar"), .width(32)) shifter_3 (.in(A), .\dist (B[4:0]), .out(shifter_3_out));
  Shifter #(.shift("rl"), .width(32)) shifter_4 (.in(A), .\dist (B[4:0]), .out(shifter_4_out));
  Shifter #(.shift("rr"), .width(32)) shifter_5 (.in(A), .\dist (B[4:0]), .out(shifter_5_out));
  Comparator #(.mode("unsigned")) comparator_1 (
    .a(A[7:0]), .b(B[7:0]), .gt(comparator_1_gt[0]), .eq(comparator_1_gt[1]), .lt(comparator_1_gt[2]));
  Comparator #(.mode("unsigned"), .width(16)) comparator_2 (
    .a(A[15:0]), .b(B[15:0]), .gt(comparator_2_gt[0]), .eq(comparator_2_gt[1]), .lt(comparator_2_gt[2]));
  Comparator #(.mode("unsigned"), .width(32)) comparator_3 (
    .a(A), .b(B), .gt(comparator_3_gt[0]), .eq(comparator_3_gt[1]), .lt(comparator_3_gt[2]));
  Comparator comparator_4 (
    .a(A[7:0]), .b(B[7:0]), .gt(comparator_4_gt[0]), .eq(comparator_4_gt[1]), .lt(comparator_4_gt[2]));
  Comparator #(.width(16)) comparator_5 (
    .a(A[15:0]), .b(B[15:0]), .gt(comparator_5_gt[0]), .eq(comparator_5_gt[1]), .lt(comparator_5_gt[2]));
  Comparator #(.width(32)) comparator_6 (
    .a(A), .b(B), .gt(comparator_6_gt[0]), .eq(comparator_6_gt[1]), .lt(comparator_6_gt[2]));
  Multiplexer multiplexer_1 (
    .in0(subtractor_1_out[8]), .in1(subtractor_1_out[16]), .out(multiplexer_1_out), .sel(MODE[0]));
  Multiplexer multiplexer_2 (.in0(adder_1_out[8]), .in1(adder_1_out[16]), .out(multiplexer_2_out), .sel(MODE[0]));
  Multiplexer #(.width(32)) multiplexer_3 (
    .in0(multiplier_1_out), .in1(multiplier_2_out), .out(multiplexer_3_out), .sel(SET_SIGNED));
  Multiplexer #(.width(32)) multiplexer_4 (
    .in0(divider_1_out), .in1(divider_2_out), .out(multiplexer_4_out), .sel(SET_SIGNED));
  Multiplexer #(.width(32)) multiplexer_5 (
    .in0(divider_1_rem), .in1(divider_2_rem), .out(multiplexer_5_out), .sel(SET_SIGNED));
  Multiplexer #(.width(3)) multiplexer_6 (
    .in0(comparator_1_gt), .in1(comparator_4_gt), .out(multiplexer_6_out), .sel(SET_SIGNED));
  Multiplexer #(.width(3)) multiplexer_7 (
    .in0(comparator_2_gt), .in1(comparator_5_gt), .out(multiplexer_7_out), .sel(SET_SIGNED));
  Multiplexer #(.width(3)) multiplexer_8 (
    .in0(comparator_3_gt), .in1(comparator_6_gt), .out(multiplexer_8_out), .sel(SET_SIGNED));
  Multiplexer multiplexer_9 (.in0(multiplexer_1_out), .in1(subtractor_1_bout), .out(BORROW_OUT), .sel(MODE[1]));
  Multiplexer multiplexer_10 (.in0(multiplexer_2_out), .in1(adder_1_cout), .out(CARRY_OUT), .sel(MODE[1]));
  Multiplexer #(.width(32)) multiplexer_11 (
    .in0(multiplexer_4_out), .in1(multiplexer_5_out), .out(multiplexer_11_out), .sel(SET_REM));
  Multiplexer #(.width(3)) multiplexer_12 (
    .in0(multiplexer_6_out), .in1(multiplexer_7_out), .out(multiplexer_12_out), .sel(MODE[0]));
  Multiplexer #(.enable("true"), .select(4), .width(32)) multiplexer_13 (
    .in0(adder_1_out), .in1(subtractor_1_out), .in2(multiplexer_3_out), .in3(multiplexer_11_out),
    .in4(and_1_out), .in5(or_1_out), .in6(xor_1_out), .in7(not_1_out), .in8(shifter_1_out),
    .in9(shifter_2_out), .in10(shifter_3_out), .in11(shifter_4_out), .in12(shifter_5_out), .out(RESULT),
    .sel(OP), .en(ALU_EN));  // open: in13, in14, in15
  Multiplexer #(.width(3)) multiplexer_14 (
    .in0(multiplexer_12_out), .in1(multiplexer_8_out), .out({LESS_OUT, EQUALS_OUT, GREATER_OUT}),
    .sel(MODE[1]));
  Comparator #(.width(32)) comparator_7 (.a(RESULT), .b({32{1'b0}}), .eq(ZERO_OUT), .lt(SIGN_OUT));  // open: gt
endmodule
